# Fritzing sketch CatDrainer5000 (saved by Fritzing 0.9.2b)

parts:
  part = ESP32S-HiLetgo [part_number=ESP32S-HiLetgo]
  Laser_Diode = LD
  sg-90_servo = Basic Servo

nets:
  N1: part.GPIO32, Laser_Diode.anode
  N2: part.GPIO25, sg-90_servo.pulse
  GND: part.GND, Laser_Diode.cathode, sg-90_servo.gnd
  VIN: part.VIN, sg-90_servo.vcc

custom parts:
  ESP32S-HiLetgo: HiLetgo ESP-WROOM-32 ESP32 ESP-32S Development Board 2.4GHz Dual-Mode WiFi + Bluetooth Dual Cores Microcontroller The ESP32 integrated with Antenna switches, RF Balun, power amplifiers, low-noise amplifiers, filters, and management modules, and the entire solution occupies the least area of PCB. 2.4 GHz Wi-Fi plus Bluetooth dual-mode chip, with TSMC Ultra-low power consumption 40nm technology,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
  LD: A Generic Red Dot Laser Diode Module (~5mW)
